# Fritzing sketch button_led (saved by Fritzing 0.9.3b)
breadboards: 1

parts:
  Raspberry_Pi_1 = Raspberry Pi 3 [part_number=RPI-3-V1.2]
  S1 = Pushbutton [package="[THT]"]
  R1 = Resistor [tolerance=±5% resistance=330 package=THT]
  LED1 = LED - 5mm [color="Red (633nm)" package="5 mm [THT]"]

nets:
  N1: Raspberry_Pi_1.GPIO17, S1.Pin_1, S1.Pin_2
  N2: Raspberry_Pi_1.GPIO27, R1.Pin_0
  N3: Raspberry_Pi_1.GND, S1.Pin_3, S1.Pin_4, LED1.cathode
  N4: R1.Pin_1, LED1.anode

notes:
  Button auf Pin 11 mit PULL UP Widerstand
  LED Eingang auf Pin 13 mit Vorwiderstand 330Ohm
