# Fritzing sketch rpi_arduino (saved by Fritzing 0.9.3b)
breadboards: 1

parts:
  Raspberry_Pi_1 = Raspberry Pi 3 [part_number=RPI-3-V1.2]  # not connected
  R1 = Resistor [tolerance=±5% resistance=330 package=THT]
  LED1 = LED - 5mm [color="Red (633nm)" package="5 mm [THT]"]
  Bauteil1 = Arduino Uno (Rev3)
  R2 = Rotary Potentiometer (Small) [maximum_resistance=100kΩ package=THT]

nets:
  N1: R1.Pin_0, Bauteil1.D9_PWM
  N2: R1.Pin_1, LED1.anode
  N3: LED1.cathode, Bauteil1.GND, R2.leg1
  N4: Bauteil1.A0, R2.wiper
  N5: Bauteil1.5V, R2.leg2

notes:
  Connect Raspberry Pi and Arduino via USB
